// Logisim project cpu.circ as structural Verilog: 1 circuit, main circuit main
module main (
  input  [31:0] INSTRUCTION,
  input  CLOCK,
  input  in_3,
  input  in_4,
  output [31:0] PROGRAM_COUNTER,
  output [31:0] ra,
  output [31:0] sp,
  output [31:0] t0,
  output [31:0] t1,
  output [31:0] t2,
  output [31:0] s0,
  output [31:0] s1,
  output [31:0] a0,
  output [31:0] out_14,
  output [31:0] out_15
);

  wire comparator_1_eq, DMEM_p1, DMEM_p4;
  wire [3:0] ALu_Sel;
  wire [31:0] adder_1_out, imm_ext, Mem_out, RegFile_read_data_1;

  Adder #(.width(32)) adder_1 (.a(PROGRAM_COUNTER), .b(32'h4), .out(adder_1_out));  // open: cin, cout
  Register #(.width(32)) PC (.D(adder_1_out), .clk(CLOCK), .Q(PROGRAM_COUNTER), .clr(in_3));  // open: en
  assign imm_ext = {{20{INSTRUCTION[31]}}, INSTRUCTION[31:20]};  // Bit_Extender bit_extender_1
  Multiplexer #(.width(32), .enable("false")) multiplexer_1 (
    .in0(Mem_out), .in1(out_14), .out(out_15), .sel(INSTRUCTION[4]));
  regfile_main RegFile (
    .rd(INSTRUCTION[11:7]), .Read_Data_1(RegFile_read_data_1), .ra(ra), .sp(sp), .t0(t0), .t1(t1), .t2(t2),
    .s0(s0), .s1(s1), .a0(a0), .rs1(INSTRUCTION[19:15]), .Write_Data(out_15), .RegWEn(in_4), .clk(CLOCK));  // open: rs2, Read_Data_2
  Comparator #(.width(10)) comparator_1 (
    .a({INSTRUCTION[14:12], INSTRUCTION[6:0]}), .b(10'h13), .eq(comparator_1_eq));  // open: gt, lt
  alu Arithmetic_Logic_Unit (.Result(out_14), .ALUSel(ALu_Sel), .A(RegFile_read_data_1), .B(imm_ext));
  assign ALu_Sel = comparator_1_eq ? 4'b0000 : 4'bz;  // Controlled_Buffer controlled_buffer_1
  // mem_main DMEM: pin names not known; wires that end beside it: DMEM_p1, DMEM_p1, CLOCK, DMEM_p4, Mem_out

  // Other names for the same wires on the sheet: opcode[6:0] = INSTRUCTION[6:0]; funct3[2:0] = INSTRUCTION[14:12];
  //   ALU_out[31:0] = out_14; clk = CLOCK; rd[4:0] = INSTRUCTION[11:7]; rs1[4:0] = INSTRUCTION[19:15];
  //   imm[11:0] = INSTRUCTION[31:20]

  // Notes on the sheet:
  //   Output
  //   IMEM (do **NOT** move this)
  //   Inputs
  //   It is OK to move the PC, RegFile, ALU, and MEM to wherever is most convenient for you when constructing your CPU, and to delete this text
  //   Inputs/Outputs for testing. Do **NOT** move these.
endmodule
